# Fritzing sketch Untitled Sketch (saved by Fritzing 0.9.4)
breadboards: 1

parts:
  M1 = STM32F103C8T6 blue mini board
  7_Segment1 = 7 Segment Display
  S1 = Pushbutton [package="[THT]"]
  S2 = Pushbutton [package="[THT]"]
  R1 = Resistor [tolerance=±5% resistance=220 package=THT]
  R2 = Resistor [tolerance=±5% resistance=220 package=THT]

nets:
  N1: M1.G, R1.Pin_1, R2.Pin_1
  N2: M1.3.3V, S1.Pin_1, S1.Pin_2, S2.Pin_1, S2.Pin_2
  N3: M1.A0, M1.A1, M1.A4, M1.A5, M1.A6, 7_Segment1.Segment_A, 7_Segment1.Segment_F, 7_Segment1.common_anode#3, 7_Segment1.Segment_E, 7_Segment1.Segment_G, 7_Segment1.Segment_B, 7_Segment1.common_anode#16
  N4: M1.A2, 7_Segment1.common_anode#12
  N5: M1.A3, 7_Segment1.Segment_DP, 7_Segment1.Segment_D
  N6: M1.B0, S1.Pin_3, S1.Pin_4, R1.Pin_0
  N7: M1.B1, S2.Pin_3, S2.Pin_4, R2.Pin_0
